// Logisim project Three_bit_multiplier.circ as structural Verilog: 1 circuit, main circuit main
module main (
  input  in_1,
  input  in_2,
  input  in_3,
  input  in_4,
  input  in_5,
  input  in_6,
  output out_7
);

  wire adder_1_p2, and_7_out, and_8_out;

  // AND_Gate and_1 has open pins: in1=in_5, in3=in_1, out=open
  // AND_Gate and_2 has open pins: in1=in_6, in2=in_1, out=open
  // AND_Gate and_3 has open pins: in1=in_4, in3=in_1, out=open
  // AND_Gate and_4 has open pins: in0=in_5, in3=in_2, out=open
  // AND_Gate and_5 has open pins: in1=in_6, in3=in_2, out=open
  // AND_Gate and_6 has open pins: in1=in_6, in2=in_3, out=open
  and and_7 (and_7_out, in_4, in_2);
  and and_8 (and_8_out, in_5, in_3);
  and and_9 (out_7, in_4, in_3);
  // Adder #(.width(1)) adder_1: pin names not known; wires that end beside it: and_8_out, adder_1_p2, and_7_out
endmodule
